# Fritzing sketch Partie Electronique (saved by Fritzing 0.9.9b)
breadboards: 1

parts:
  Composant1 = Arduino Mega 2560 (Rev3)
  Pololu_A1 = Pololu A4988 [package=SO16]
  Pololu_A2 = Pololu A4988 [package=SO16]
  Pololu_A3 = Pololu A4988 [package=SO16]
  Pololu_A4 = Pololu A4988 [package=SO16]
  M5 = Stepper Motor - Bipolar
  M6 = Stepper Motor - Bipolar
  M7 = Stepper Motor - Bipolar
  M8 = Stepper Motor - Bipolar
  C5 = Capacitor Polarized [package=panasonic_d]
  C6 = Capacitor Polarized [package=panasonic_d]
  C7 = Capacitor Polarized [package=panasonic_d]
  C8 = Capacitor Polarized [package=panasonic_d]
  SW1 = ENCODER_RGB_CA [package=encoder_led_3]
  SW2 = ENCODER_RGB_CA [package=encoder_led_3]
  SW3 = ENCODER_RGB_CA [package=encoder_led_3]
  SW4 = ENCODER_RGB_CA [package=encoder_led_3]
  VCC1 = Battery block 9V  # not connected
  VCC2 = Battery block 9V
  VCC3 = Battery block 9V

nets:
  N1: Composant1.D19/RX1, SW4.C
  N2: Composant1.D18/TX1, SW3.C
  N3: Composant1.D2_PWM, SW2.C
  N4: Composant1.D22, Pololu_A1.DIR
  N5: Composant1.D23, Pololu_A1.STEP
  N6: Composant1.D24, SW1.B
  N7: Composant1.D26, SW2.A
  N8: Composant1.D29, Pololu_A2.STEP
  N9: Composant1.D31, Pololu_A3.STEP
  N10: Composant1.D32, SW3.A
  N11: Composant1.D34, SW4.A
  N12: Composant1.D37, Pololu_A4.STEP
  N13: Composant1.D41, Pololu_A3.MS1
  N14: Composant1.D43, Pololu_A4.MS1
  N15: Composant1.D45, Pololu_A4.MS2
  N16: Composant1.D46, Pololu_A2.DIR
  N17: Composant1.D47, Pololu_A1.MS2
  N18: Composant1.D49, Pololu_A1.MS3, Pololu_A2.MS1
  N19: Composant1.D51, Pololu_A2.MS2
  N20: Pololu_A1.RESET, Pololu_A1.SLEEP
  N21: Pololu_A1.GND#8, Pololu_A2.GND#8, Pololu_A3.GND#8
  VDD: Pololu_A1.VDD, Pololu_A2.VDD, Pololu_A3.VDD
  N22: Pololu_A1.1B, M8.D
  N23: Pololu_A1.1A, M8.B
  N24: Pololu_A1.2A, M8.C
  N25: Pololu_A1.2B, M8.A
  N26: Pololu_A1.GND#14, Pololu_A2.GND#14, VCC3.-
  N27: Pololu_A1.VMOT, Pololu_A2.VMOT, VCC2.+
  N28: Pololu_A2.RESET, Pololu_A2.SLEEP
  N29: Pololu_A2.1B, M7.D
  N30: Pololu_A2.1A, M7.B
  N31: Pololu_A2.2A, M7.C
  N32: Pololu_A2.2B, M7.A
  N33: Pololu_A3.RESET, Pololu_A3.SLEEP
  N34: Pololu_A3.1B, M6.D
  N35: Pololu_A3.1A, M6.B
  N36: Pololu_A3.2A, M6.C
  N37: Pololu_A3.2B, M6.A
  N38: Pololu_A3.GND#14, Pololu_A4.GND#14, C5.-, C6.-, C7.-, C8.-
  N39: Pololu_A3.VMOT, Pololu_A4.VMOT, C5.+, C6.+, C7.+, C8.+
  N40: Pololu_A4.RESET, Pololu_A4.SLEEP
  N41: Pololu_A4.VDD, SW1.+
  N42: Pololu_A4.1B, M5.D
  N43: Pololu_A4.1A, M5.B
  N44: Pololu_A4.2A, M5.C
  N45: Pololu_A4.2B, M5.A
  N46: SW3.-B, SW4.-B

// code stored in the sketch: TDCR.ino

#include <Arduino.h>
#include "A4988.h" 
// Stepper Motor 1 configuration [21]
// using a 200-step motor (most common)
#define MOTOR_STEPS 200
// configure the pins connected
#define DIR 23
#define STEP 22
#define MS1 46
#define MS2 47
#define MS3 48
A4988 stepper1(MOTOR_STEPS, DIR, STEP, MS1, MS2, MS3);
float i=27.5; // angle increment index
float alpha=1.00765 ; // 1.00765,1.1085 Segment 1 Actuation Compensation Factor1
float beta=1; //Compensation Factor2
float Ay2;
float Ax2;
float Ay1;
float Ax1;
// Rotary endoder 1 setup
volatile boolean TurnDetected; // need volatile for Interrupts
volatile boolean rotationdirection; // CW or CCW rotation
const int PinCLK=3; // Generating interrupts using CLK signal
const int PinDT=24; // Reading DT signal
const int PinSW=25; // Reading Push Button switch
const int interruptpin1=3 ; // Interrupt pin1 number
int RotaryPosition=0; // To store Stepper Motor Position
int PrevPosition; // Previous Rotary position Value to check accuracy
float AnglesToRotate=0; // How much angle to move Stepper
int encodata;
float Rx2; // Segment 2 x rotation angle
float Ry2; // Segment 2 y rotation angle
float Rx1; // Segment 1 x rotation angle
float Ry1; // Segment 1 y rotation angle
// Interrupt routine runs if CLK goes from HIGH to LOW
void isr () {
 delay(4); // delay for Debouncing
 encodata=digitalRead(PinCLK);
 if (digitalRead(PinCLK))
 rotationdirection= digitalRead(PinDT);
 else
 rotationdirection= !digitalRead(PinDT);
 TurnDetected = true;
}
// Stepper Motor 2 configuration
// using a 200-step motor (most common)
#define MOTOR_STEPS 200
// configure the pins connected
#define DIR2 28
#define STEP2 29
#define MS1_2 49
#define MS2_2 50
#define MS3_2 51
A4988 stepper2(MOTOR_STEPS, DIR2, STEP2, MS1_2, MS2_2, MS3_2);
int i2=20; // angle increment index
// Rotary endoder 2 setup
volatile boolean TurnDetected2; // need volatile for Interrupts
volatile boolean rotationdirection2; // CW or CCW rotation
const int PinCLK2=2; // Generating interrupts using CLK signal
const int PinDT2=26; // Reading DT signal
const int PinSW2=27; // Reading Push Button switch
const int interruptpin2=PinCLK2 ; // Interrupt pin1 number
int RotaryPosition2=0; // To store Stepper Motor Position
int PrevPosition2; // Previous Rotary position Value to check accuracy
float AnglesToRotate2=0; // How much angle to move Stepper
int encodata2;
// Interrupt routine runs if CLK goes from HIGH to LOW
void isr2 () {
 delay(4); // delay for Debouncing
 encodata2=digitalRead(PinCLK2);
 if (digitalRead(PinCLK2))
 rotationdirection2= digitalRead(PinDT2);
 else
 rotationdirection2= !digitalRead(PinDT2);
 TurnDetected2 = true;
}
// Stepper Motor 3 configuration
// using a 200-step motor (most common)
//#define MOTOR_STEPS 200
// configure the pins connected
#define DIR3 31
#define STEP3 30
#define MS1_3 40
#define MS2_3 41
#define MS3_3 42
A4988 stepper3(MOTOR_STEPS, DIR3, STEP3, MS1_3, MS2_3, MS3_3);
int i3=20; // angle increment index
// Rotary endoder 3 setup
volatile boolean TurnDetected3; // need volatile for Interrupts
volatile boolean rotationdirection3; // CW or CCW rotation
const int PinCLK3=18; // Generating interrupts using CLK signal
const int PinDT3=32; // Reading DT signal
const int PinSW3=33; // Reading Push Button switch
const int interruptpin3=PinCLK3 ; // Interrupt pin1 number
int RotaryPosition3=0; // To store Stepper Motor Position
int PrevPosition3; // Previous Rotary position Value to check accuracy
float AnglesToRotate3=0; // How much angle to move Stepper
int encodata3;
// Interrupt routine runs if CLK goes from HIGH to LOW
void isr3 () {
 delay(4); // delay for Debouncing
 encodata3=digitalRead(PinCLK3);
 if (digitalRead(PinCLK3))
 rotationdirection3= digitalRead(PinDT3);
 else
 rotationdirection3= !digitalRead(PinDT3);
 TurnDetected3 = true;
}
// Stepper Motor 4 configuration
// using a 200-step motor (most common)
//#define MOTOR_STEPS 200
// configure the pins connected
#define DIR4 37
#define STEP4 36
#define MS1_4 43
#define MS2_4 44
#define MS3_4 45
A4988 stepper4(MOTOR_STEPS, DIR4, STEP4, MS1_4, MS2_4, MS3_4);
int i4=20; // angle increment index
// Rotary endoder 4 setup
volatile boolean TurnDetected4; // need volatile for Interrupts
volatile boolean rotationdirection4; // CW or CCW rotation
const int PinCLK4=19; // Generating interrupts using CLK signal
const int PinDT4=34; // Reading DT signal
const int PinSW4=35; // Reading Push Button switch
const int interruptpin4=PinCLK4 ; // Interrupt pin1 number
int RotaryPosition4=0; // To store Stepper Motor Position
int PrevPosition4; // Previous Rotary position Value to check accuracy
float AnglesToRotate4=0; // How much angle to move Stepper
int encodata4;
// Interrupt routine runs if CLK goes from HIGH to LOW
void isr4 () {
 delay(4); // delay for Debouncing
 encodata4=digitalRead(PinCLK4);
 if (digitalRead(PinCLK4))
 rotationdirection4= digitalRead(PinDT4);
 else
 rotationdirection4= !digitalRead(PinDT4);
 TurnDetected4 = true;
}
void setup() {
 // Set target motor RPM to 1RPM and microstepping to 1 (full step mode)
 stepper1.begin(180, 16);
 //Rotary encoder 1 setup
 pinMode(PinCLK,INPUT);
pinMode(PinDT,INPUT); 
pinMode(PinSW,INPUT);
digitalWrite(PinSW, HIGH); // Pull-Up resistor for switch
// Rotary encoder 2 setup
stepper2.begin(180, 16);
pinMode(PinCLK2,INPUT);
pinMode(PinDT2,INPUT); 
pinMode(PinSW2,INPUT);
digitalWrite(PinSW2, HIGH); // Pull-Up resistor for switch
//attachInterrupt (digitalPinToInterrupt(PinCLK2),isr2,FALLING); // interrupt 0 
//always connected to pin 2 on Arduino UNO
// Rotary encoder 3 setup
stepper3.begin(180, 16);
pinMode(PinCLK3,INPUT);
pinMode(PinDT3,INPUT); 
pinMode(PinSW3,INPUT);
digitalWrite(PinSW3, HIGH); // Pull-Up resistor for switch
// Rotary encoder 4 setup
stepper4.begin(180, 16);
pinMode(PinCLK4,INPUT);
pinMode(PinDT4,INPUT); 
pinMode(PinSW4,INPUT);
digitalWrite(PinSW4, HIGH); // Pull-Up resistor for switch
attachInterrupt (digitalPinToInterrupt(PinCLK2),isr2,CHANGE); // interrupt 0 always 
//connected to pin 2 on Arduino UNO
attachInterrupt (digitalPinToInterrupt(PinCLK),isr,CHANGE); // interrupt 0 always 
//connected to pin 2 on Arduino UNO
attachInterrupt (digitalPinToInterrupt(PinCLK3),isr3,CHANGE); // interrupt 3 setup 
attachInterrupt (digitalPinToInterrupt(PinCLK4),isr4,CHANGE); // interrupt 3 setup 
Serial.begin(9600); // opens serial port, sets data rate to 9600 bps
}



void loop() {
 if (!(digitalRead(PinSW))) { // check if button is pressed
 if (RotaryPosition == 0) { // check if button was already pressed
 } 
 else {
 stepper1.move(-(RotaryPosition*i));
 RotaryPosition=0; // Reset position to ZERO
 }
 }
if (TurnDetected3 ||TurnDetected || TurnDetected2|| TurnDetected4) {
if (TurnDetected3) {
PrevPosition3 = RotaryPosition3; // Save previous position in variable
 if (rotationdirection3) {
 RotaryPosition3=RotaryPosition3-1;} // decrase Position by 1
 else {
 RotaryPosition3=RotaryPosition3+1;} // increase Position by 1
 TurnDetected3 = false; // do NOT repeat IF loop until new rotation detected
 // Which direction to move Stepper motor
 if ((RotaryPosition3 + 1) == PrevPosition3) { // Move motor CCW
 
 AnglesToRotate3=-i*1.8/16;
 //stepper3.rotate(AnglesToRotate3);
 }
 else if ((PrevPosition3 + 1) == RotaryPosition3) { // Move motor CW
 AnglesToRotate3=i*1.8/16;
 // stepper3.rotate(AnglesToRotate3);
 }
 else {AnglesToRotate3=0 ;}
// Serial print encoder 
Serial.print("encodata3:");
Serial.println(encodata3,DEC); 
}
if (TurnDetected) {
 PrevPosition = RotaryPosition; // Save previous position in variable
 if (rotationdirection) {
 RotaryPosition=RotaryPosition-1;} // decrase Position by 1
 else {
 RotaryPosition=RotaryPosition+1;} // increase Position by 1
 TurnDetected = false; // do NOT repeat IF loop until new rotation detected
 // Which direction to move Stepper motor
 if ((RotaryPosition + 1) == PrevPosition) { // Move motor CCW
 
 AnglesToRotate=-i*1.8/16;
 // stepper1.rotate(AnglesToRotate);
 }
 else if ((PrevPosition + 1) == RotaryPosition) { // Move motor CW
 AnglesToRotate=i*1.8/16;
 // stepper1.rotate(AnglesToRotate);
 }
 else {AnglesToRotate=0 ;} 
// Serial print encoder
 Serial.print("encodata1:");
Serial.println(encodata,DEC);
 }
if (TurnDetected2) {
 PrevPosition2 = RotaryPosition2; // Save previous position in variable
 if (rotationdirection2) {
 RotaryPosition2=RotaryPosition2-1;} // decrase Position by 1
 else {
 RotaryPosition2=RotaryPosition2+1;} // increase Position by 1
 TurnDetected2 = false; // do NOT repeat IF loop until new rotation detected
 // Which direction to move Stepper motor
 if ((RotaryPosition2 + 1) == PrevPosition2) { // Move motor CCW
 
 AnglesToRotate2=-i*1.8/16;
 //stepper2.rotate(AnglesToRotate2);
 }
 else if ((PrevPosition2 + 1) == RotaryPosition2) { // Move motor CW
 AnglesToRotate2=i*1.8/16;
 // stepper2.rotate(AnglesToRotate2);
 }
 else {AnglesToRotate2=0 ;}
// Serial print encoder
 
Serial.print("encodata2:");
Serial.println(encodata2,DEC);
 }
if (TurnDetected4) {
PrevPosition4 = RotaryPosition4; // Save previous position in variable
 if (rotationdirection4) {
 RotaryPosition4=RotaryPosition4-1;} // decrase Position by 1
 else {
 RotaryPosition4=RotaryPosition4+1;} // increase Position by 1
 TurnDetected4 = false; // do NOT repeat IF loop until new rotation detected
 // Which direction to move Stepper motor
 if ((RotaryPosition4 + 1) == PrevPosition4) { // Move motor CCW
 
 AnglesToRotate4=-i*1.8/16;
 //stepper4.rotate(AnglesToRotate4);
 }
 else if ((PrevPosition4 + 1) == RotaryPosition4) { // Move motor CW
 AnglesToRotate4=i*1.8/16;
 // stepper4.rotate(AnglesToRotate4);
 }
 else {AnglesToRotate4=0 ;}
 
// Serial print encoder
Serial.print("encodata4:");
Serial.println(encodata4,DEC); 
}
//Rx2=(AnglesToRotate3+AnglesToRotate*0.866025+AnglesToRotate2*0.5)*16/1.8;
//Ry2=(AnglesToRotate4+AnglesToRotate2*0.866025-0.5*AnglesToRotate)*16/1.8;
//Ry1=AnglesToRotate2*16/1.8;
//Rx1=AnglesToRotate*16/1.8;
Rx2=(AnglesToRotate3+AnglesToRotate*0.866025+AnglesToRotate2*0.5);
Ry2=(AnglesToRotate4+AnglesToRotate2*0.866025-0.5*AnglesToRotate);
Ry1=AnglesToRotate2-alpha*0.5*AnglesToRotate4*0.866025-(alpha*beta)*0.5*AnglesToRotate3*0.5;
Rx1=AnglesToRotate-alpha*0.5*AnglesToRotate3*0.866025+(alpha*beta)*0.5*AnglesToRotate4*0.5;
int j=6;
//for(int s=0; s<i; s++)
//{stepper1.rotate(Ry2/i);
// stepper2.rotate(Rx2/i);
// stepper3.rotate(Ry1/i);
// stepper4.rotate(Rx1/i); 
//}
Ay2=Ry2/j;
Ax2=Rx2/j;
Ay1=Ry1/j;
Ax1=Rx1/j;
for(int s=0; s<j; s++)
{stepper1.rotate(Ay2);
stepper2.rotate(Ax2);
stepper3.rotate(Ay1);
stepper4.rotate(Ax1); 
}
AnglesToRotate=0; // reset angles to rotate to zero
AnglesToRotate2=0;
AnglesToRotate3=0;
AnglesToRotate4=0;
}
}
